# Fritzing sketch Takhomasak_Speedway (saved by Fritzing 1.0.5)

parts:
  uPesy_ESP32_Wroom_DevKit1 = uPesy ESP32 Wroom DevKit v2
  S1 = Round Pushbutton
  S2 = Round Pushbutton
  S3 = Round Pushbutton
  S4 = Round Pushbutton
  LED1 = LEDs [package=led10mm]
  LED2 = LEDs [package=led10mm]
  LED4 = LEDs [package=led10mm]
  R2 = Resistor [tolerance=±5% resistance=220 package="1206 [SMD]"]
  R3 = Resistor [tolerance=±5% resistance=220 package="1206 [SMD]"]
  R4 = Resistor [tolerance=±5% resistance=220 package="1206 [SMD]"]
  JP2 = Header 6 [package=molex-1x6-ra]
  JP3 = Header 6 [package=molex-1x6-ra]
  JP1 = Header 6 [package=molex-1x6-ra]
  JP14 = Header 6 [package=molex-1x6-ra]
  JP15 = Header 6 [package=molex-1x6-ra]
  JP16 = Header 6 [package=molex-1x6-ra]

nets:
  N1: uPesy_ESP32_Wroom_DevKit1.GPIO23, JP14.DIN, JP15.DIN, JP16.DIN
  N2: uPesy_ESP32_Wroom_DevKit1.GPIO22, JP2.SCL, JP3.SCL, JP1.SCL
  N3: uPesy_ESP32_Wroom_DevKit1.GPIO21, JP2.SDA, JP3.SDA, JP1.SDA
  N4: uPesy_ESP32_Wroom_DevKit1.GPIO19, JP14.CLK, JP15.CLK, JP16.CLK
  N5: uPesy_ESP32_Wroom_DevKit1.GPIO18, JP1.XSHUT
  N6: uPesy_ESP32_Wroom_DevKit1.GPIO5, JP2.XSHUT
  N7: uPesy_ESP32_Wroom_DevKit1.GPIO16, R2.Pin_1
  N8: uPesy_ESP32_Wroom_DevKit1.GPIO4, JP3.XSHUT
  N9: uPesy_ESP32_Wroom_DevKit1.GPIO15, R4.Pin_1
  VCC: uPesy_ESP32_Wroom_DevKit1.3V3, JP2.VCC, JP3.VCC, JP1.VCC
  GND: uPesy_ESP32_Wroom_DevKit1.GND#16, LED1.C, LED2.C, LED4.C, JP2.GND, JP3.GND, JP1.GND
  GND_2: uPesy_ESP32_Wroom_DevKit1.GND#17, S1.leg1, S2.leg1, S3.leg1, S4.leg1, JP14.GND, JP15.GND, JP16.GND
  VCC_2: uPesy_ESP32_Wroom_DevKit1.5V, JP14.VCC, JP15.VCC, JP16.VCC
  N10: uPesy_ESP32_Wroom_DevKit1.GPIO13, JP15.CS
  N11: uPesy_ESP32_Wroom_DevKit1.GPIO12, JP14.CS
  N12: uPesy_ESP32_Wroom_DevKit1.GPIO14, R3.Pin_1
  N13: uPesy_ESP32_Wroom_DevKit1.GPIO27, S2.leg0
  N14: uPesy_ESP32_Wroom_DevKit1.GPIO26, S4.leg0
  N15: uPesy_ESP32_Wroom_DevKit1.GPIO25, S3.leg0
  N16: uPesy_ESP32_Wroom_DevKit1.GPIO33, S1.leg0
  N17: uPesy_ESP32_Wroom_DevKit1.GPIO32, JP16.CS
  N18: LED1.A, R4.Pin_0
  N19: LED2.A, R2.Pin_0
  N20: LED4.A, R3.Pin_0

custom parts:
  uPesy ESP32 Wroom DevKit v2: ESP32 development board that is 100% breadboard compatible
  Header 6: Header 6 Standard 6-pin 0.1 header. Use with straight break away headers (SKU : PRT-00116), right angle break away headers (PRT-00553), swiss pins (PRT-00743), machine pins (PRT-00117), and female headers (PRT-00115). Molex polarized connector foot print use with SKU : PRT-08094 with associated crimp pins and housings. NOTES ON THE VARIANTS LOCK and LOCK_LONGPADS... This footprint was designed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
  Header 6: Header 6 Standard 6-pin 0.1 header. Use with straight break away headers (SKU : PRT-00116), right angle break away headers (PRT-00553), swiss pins (PRT-00743), machine pins (PRT-00117), and female headers (PRT-00115). Molex polarized connector foot print use with SKU : PRT-08094 with associated crimp pins and housings. NOTES ON THE VARIANTS LOCK and LOCK_LONGPADS... This footprint was designed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
